# Fritzing sketch nano_bird_schematic (saved by Fritzing 0.9.3b)
circuit board: 10.1622cm x 2.95877cm
breadboards: 1

parts:
  Part1 = Arduino Nano (Rev3.0) (ICSP)
  Grove1 = Grove OLED 128x96
  S1 = Pushbutton [package="[THT]"]

nets:
  GND: Part1.GND, Grove1.GND, S1.Pin_1, S1.Pin_2
  N1: Part1.D2, S1.Pin_3, S1.Pin_4
  VIN: Part1.VIN, Grove1.VCC
  N2: Part1.A5, Grove1.SCL
  N3: Part1.A4, Grove1.SDA
